# Fritzing sketch Sistemas de Automatización de Alarma y Luces (saved by Fritzing 0.9.3b)
breadboards: 1

parts:
  Componente1 = Arduino Mega 2560 (Rev3)
  R1 = Resistor [tolerance=±5% resistance=220 package=THT]
  LED1 = LED - 5mm [color="Red (633nm)" package="5 mm [THT]"]
  LED2 = LED - 5mm [color="Red (633nm)" package="5 mm [THT]"]
  J1 = Piezo Speaker

nets:
  N1: Componente1.GND, R1.Pin_0, J1.pin1
  N2: Componente1.D13_PWM, LED2.anode
  N3: Componente1.D12_PWM, LED1.anode
  N4: Componente1.D11_PWM, J1.pin2
  N5: R1.Pin_1, LED1.cathode, LED2.cathode

notes:
  SENSOR
  PIR
  RELAY
  KEYPAD
  CONECTOR I2C PARA EL MANEJO
  DEL LCD
